# Fritzing sketch gps (saved by Fritzing 0.9.2b)
circuit board: 19.0264cm x 13.4812cm
breadboards: 1

parts:
  Часть1 = DeuLigne 1.1 - The Snootlab's LCD shield for Arduino
  GPS = GP-2106 [package=gp-2106]
  microSD = SparkFun - microSD Transflash
  Расширитеь_пинов_Отсчет_с_0_права_низ = Packages: [package=tssop28-groundpad]
  Часть2 = Arduino Uno (Rev3)

nets:
  +5V: Часть1.+5V, Часть2.5V
  GND: Часть1.GND, GPS.GND, Часть2.GND
  N1: Часть1.D9, Расширитеь_пинов_Отсчет_с_0_права_низ.XLAT
  N2: Часть1.D10_SS, Расширитеь_пинов_Отсчет_с_0_права_низ.SIN
  N3: Часть1.D1_TX, Расширитеь_пинов_Отсчет_с_0_права_низ.OUT8
  N4: Часть1.D2, Расширитеь_пинов_Отсчет_с_0_права_низ.OUT7
  N5: Часть1.D4, Расширитеь_пинов_Отсчет_с_0_права_низ.OUT3
  N6: Часть1.D5, Расширитеь_пинов_Отсчет_с_0_права_низ.OUT4
  N7: Часть1.D6, Расширитеь_пинов_Отсчет_с_0_права_низ.OUT5
  N8: Часть1.D7, Расширитеь_пинов_Отсчет_с_0_права_низ.OUT6
  N9: GPS.RX, Часть2.D3_PWM
  N10: GPS.TX, Часть2.D5_PWM
  VCC: GPS.VCC, Часть2.3V3
  N11: microSD.CS, Часть2.D4

notes:
  розовый
  расширитель SCL
  коричневый
  расширитель ADS
  расширитель
  земля
  расширитель
  5v
  DO - MOSI
  CD - MISO
  на один пин меньше
  чем на моем расширителе (делай отсчет справа)
